// Logisim project piped.circ as structural Verilog: 13 circuits, main circuit main
module main (
);

  wire and_1_out, Clock, control_1_alusrc, control_1_branch, control_1_memread, control_1_memtoreg,
       control_1_memwrite, control_1_regdst, control_1_regwrite, ex_ctrl_1_alusrc_read,
       ex_ctrl_1_regdst_read, ex_mem_1_zero_read, m_ctrl_1_branch_read, m_ctrl_1_memread_read,
       m_ctrl_1_memwrite_read, m_ctrl_2_branch_read, m_ctrl_2_memread_read, m_ctrl_2_memwrite_read,
       mips_alu_1_p4, registerfile_1_p2, wb_ctrl_1_memtoreg_read, wb_ctrl_1_regwrite_read,
       wb_ctrl_2_memtoreg_read, wb_ctrl_2_regwrite_read, wb_ctrl_3_memtoreg_read;
  wire [1:0] control_1_aluop, ex_ctrl_1_aluop_read, forwarding_uni_1_forward_a, forwarding_uni_1_forward_b;
  wire [3:0] alu_control_1_out_3;
  wire [4:0] ex_mem_1_write_register_read, id_ex_1_write_register_read, id_ex_1_write_register_read_2,
       instructiondecode_1__11_15, instructiondecode_1__16_20, instructiondecode_1__21_25, multiplexer_3_out,
       register_1_q, registerfile_1_p3;
  wire [5:0] instructiondecode_1__26_31;
  wire [15:0] instructiondecode_1__0_15;
  wire [23:0] bit_extender_2_out;
  wire [31:0] adder_1_out, adder_2_out, bit_extender_1_out, ex_mem_1_branch_address_read, ex_mem_1_out_10,
       ex_mem_1_register_read_data_2_read, id_ex_1_immediate_field_write_2, id_ex_1_incremented_pc_read,
       id_ex_1_register_read_data_1_write_2, id_ex_1_register_read_data_2_read, if_id_1_out_4, if_id_1_out_5,
       mem_wb_1_alu_result_read, mem_wb_1_read_data_write_2, mips_alu_1_p5, mips_ram_1_p6,
       mipsprogramrom_1_p2, mipsprogramrom_1_p3, multiplexer_1_out, multiplexer_2_out, multiplexer_4_out,
       multiplexer_5_out, PC_q, registerfile_1_p6, registerfile_1_p7, shifter_1_out;

  Clock clock_1 (.out(Clock));
  Register #(.width(32)) PC (.D(multiplexer_1_out), .Q(PC_q), .clk(Clock));  // open: en, clr
  Multiplexer #(.width(32), .enable("false")) multiplexer_1 (
    .in0(adder_1_out), .in1(ex_mem_1_branch_address_read), .out(multiplexer_1_out), .sel(and_1_out));
  Adder #(.width(32)) adder_1 (.a(PC_q), .b(32'h4), .out(adder_1_out));  // open: cin, cout
  // MIPSProgramROM mipsprogramrom_1: pin names not known; wires that end beside it: PC_q, mipsprogramrom_1_p2, mipsprogramrom_1_p3
  IF_ID if_id_1 (
    .in_1(adder_1_out), .in_2(mipsprogramrom_1_p2), .out_4(if_id_1_out_4), .out_5(if_id_1_out_5),
    .Clock(Clock));
  instructionDecode instructiondecode_1 (
    ._32_bit_instruction(if_id_1_out_5), ._26_31(instructiondecode_1__26_31),
    ._21_25(instructiondecode_1__21_25), ._16_20(instructiondecode_1__16_20),
    ._11_15(instructiondecode_1__11_15), ._0_15(instructiondecode_1__0_15));  // open: _0_5
  control control_1 (
    .Opcode(instructiondecode_1__26_31), .ALUOp(control_1_aluop), .Branch(control_1_branch),
    .MemWrite(control_1_memwrite), .MemRead(control_1_memread), .RegWrite(control_1_regwrite),
    .MemtoReg(control_1_memtoreg), .ALUSrc(control_1_alusrc), .RegDst(control_1_regdst));
  // RegisterFile registerfile_1: pin names not known; wires that end beside it: Clock, registerfile_1_p2, registerfile_1_p3, instructiondecode_1__21_25, instructiondecode_1__16_20, registerfile_1_p6, registerfile_1_p7
  assign bit_extender_1_out = {{16{instructiondecode_1__0_15[15]}}, instructiondecode_1__0_15};  // Bit_Extender bit_extender_1
  ID_EX id_ex_1 (
    .Incremented_PC_write(if_id_1_out_4), .Register_read_data_1_write(registerfile_1_p6),
    .Register_read_data_2_write(registerfile_1_p7), .Immediate_field_write(bit_extender_1_out),
    .Incremented_PC_read(id_ex_1_incremented_pc_read),
    .Register_read_data_1_write_2(id_ex_1_register_read_data_1_write_2),
    .Register_read_data_2_read(id_ex_1_register_read_data_2_read),
    .Immediate_field_write_2(id_ex_1_immediate_field_write_2),
    .Write_register_write(instructiondecode_1__16_20), .Write_register_read(id_ex_1_write_register_read),
    .Write_register_write_2(instructiondecode_1__11_15),
    .Write_register_read_2(id_ex_1_write_register_read_2), .Clock(Clock));
  Register #(.width(5)) register_1 (.D(instructiondecode_1__21_25), .Q(register_1_q), .clk(Clock));  // open: en, clr
  EX_ctrl ex_ctrl_1 (
    .RegDst_write(control_1_regdst), .ALUSOp_write(control_1_aluop), .ALUSrc_write(control_1_alusrc),
    .Clock(Clock), .RegDst_read(ex_ctrl_1_regdst_read), .ALUOp_read(ex_ctrl_1_aluop_read),
    .ALUSrc_read(ex_ctrl_1_alusrc_read));
  M_ctrl m_ctrl_1 (
    .Branch_write(control_1_branch), .MemWrite_write(control_1_memwrite), .MemRead_write(control_1_memread),
    .Clock(Clock), .Branch_read(m_ctrl_1_branch_read), .MemWrite_read(m_ctrl_1_memwrite_read),
    .MemRead_read(m_ctrl_1_memread_read));
  WB_ctrl wb_ctrl_1 (
    .RegWrite_write(control_1_regwrite), .MemtoReg_write(control_1_memtoreg), .Clock(Clock),
    .RegWrite_read(wb_ctrl_1_regwrite_read), .MemtoReg_read(wb_ctrl_1_memtoreg_read));
  Shifter #(.width(32)) shifter_1 (.in(id_ex_1_immediate_field_write_2), .\dist (5'b00010), .out(shifter_1_out));
  Multiplexer #(.width(32), .enable("false")) multiplexer_2 (
    .in0(id_ex_1_register_read_data_2_read), .in1(id_ex_1_immediate_field_write_2), .out(multiplexer_2_out),
    .sel(ex_ctrl_1_alusrc_read));
  Multiplexer #(.width(5), .enable("false")) multiplexer_3 (
    .in0(id_ex_1_write_register_read), .in1(id_ex_1_write_register_read_2), .out(multiplexer_3_out),
    .sel(ex_ctrl_1_regdst_read));
  Adder #(.width(32)) adder_2 (
    .a(id_ex_1_incremented_pc_read), .b(shifter_1_out), .out(adder_2_out));  // open: cin, cout
  Multiplexer #(.select(2), .width(32), .enable("false")) multiplexer_4 (
    .in0(id_ex_1_register_read_data_1_write_2), .in1(mipsprogramrom_1_p3),
    .in2(ex_mem_1_register_read_data_2_read), .out(multiplexer_4_out), .sel(forwarding_uni_1_forward_a));  // open: in3
  Multiplexer #(.select(2), .width(32), .enable("false")) multiplexer_5 (
    .in0(multiplexer_2_out), .in1(mipsprogramrom_1_p3), .in2(ex_mem_1_register_read_data_2_read),
    .out(multiplexer_5_out), .sel(forwarding_uni_1_forward_b));  // open: in3
  ALU_control alu_control_1 (
    .Funct_field(id_ex_1_immediate_field_write_2[5:0]), .ALUOp(ex_ctrl_1_aluop_read),
    .out_3(alu_control_1_out_3));
  // MIPS_ALU mips_alu_1: pin names not known; wires that end beside it: multiplexer_4_out, multiplexer_5_out, alu_control_1_out_3, mips_alu_1_p4, mips_alu_1_p5
  Forwarding_uni forwarding_uni_1 (
    .EX_MEM_RegWrite(wb_ctrl_2_regwrite_read), .EX_MEM_Rd(ex_mem_1_write_register_read),
    .ID_EX_Rs(register_1_q), .ID_EX_Rt(id_ex_1_write_register_read), .MEM_WB_Rd(registerfile_1_p3),
    .MEM_WB_RegWrite(wb_ctrl_3_memtoreg_read), .Forward_A(forwarding_uni_1_forward_a),
    .Forward_B(forwarding_uni_1_forward_b));
  EX_MEM ex_mem_1 (
    .Branch_address_write(adder_2_out), .Zero_write(mips_alu_1_p4),
    .Register_read_data_2_write(mips_alu_1_p5), .in_4(id_ex_1_register_read_data_2_read), .Clock(Clock),
    .Branch_address_read(ex_mem_1_branch_address_read), .Zero_read(ex_mem_1_zero_read),
    .Register_read_data_2_read(ex_mem_1_register_read_data_2_read), .out_10(ex_mem_1_out_10),
    .Write_register_write(multiplexer_3_out), .Write_register_read(ex_mem_1_write_register_read));
  M_ctrl m_ctrl_2 (
    .Branch_write(m_ctrl_1_branch_read), .MemWrite_write(m_ctrl_1_memwrite_read),
    .MemRead_write(m_ctrl_1_memread_read), .Clock(Clock), .Branch_read(m_ctrl_2_branch_read),
    .MemWrite_read(m_ctrl_2_memwrite_read), .MemRead_read(m_ctrl_2_memread_read));
  WB_ctrl wb_ctrl_2 (
    .RegWrite_write(wb_ctrl_1_regwrite_read), .MemtoReg_write(wb_ctrl_1_memtoreg_read), .Clock(Clock),
    .RegWrite_read(wb_ctrl_2_regwrite_read), .MemtoReg_read(wb_ctrl_2_memtoreg_read));
  and and_1 (and_1_out, m_ctrl_2_branch_read, ex_mem_1_zero_read);
  Bit_Extender #(.in_width(32), .out_width(24)) bit_extender_2 (
    .in(ex_mem_1_register_read_data_2_read), .out(bit_extender_2_out));
  // MIPS_RAM mips_ram_1: pin names not known; wires that end beside it: bit_extender_2_out, ex_mem_1_out_10, m_ctrl_2_memwrite_read, m_ctrl_2_memread_read, Clock, mips_ram_1_p6
  MEM_WB mem_wb_1 (
    .Read_data_write(mips_ram_1_p6), .ALU_result_write(ex_mem_1_register_read_data_2_read),
    .Read_data_write_2(mem_wb_1_read_data_write_2), .ALU_result_read(mem_wb_1_alu_result_read),
    .Write_register_read(registerfile_1_p3), .Write_register_write(ex_mem_1_write_register_read),
    .Clock(Clock));
  WB_ctrl wb_ctrl_3 (
    .RegWrite_write(wb_ctrl_2_regwrite_read), .MemtoReg_write(wb_ctrl_2_memtoreg_read), .Clock(Clock),
    .RegWrite_read(registerfile_1_p2), .MemtoReg_read(wb_ctrl_3_memtoreg_read));
  Multiplexer #(.width(32), .enable("false")) multiplexer_6 (
    .in0(mem_wb_1_alu_result_read), .in1(mem_wb_1_read_data_write_2), .out(mipsprogramrom_1_p3),
    .sel(wb_ctrl_3_memtoreg_read));
endmodule

module IF_ID (
  input  [31:0] in_1,
  input  [31:0] in_2,
  input  Clock,
  output [31:0] out_4,
  output [31:0] out_5
);

  Register #(.width(32)) Incremented_PC (.D(in_1), .Q(out_4), .clk(Clock));  // open: en, clr
  Register #(.width(32)) Fetched_instruction (.D(in_2), .Q(out_5), .clk(Clock));  // open: en, clr
endmodule

module ID_EX (
  input  [31:0] Incremented_PC_write,
  input  [31:0] Register_read_data_1_write,
  input  [31:0] Register_read_data_2_write,
  input  [31:0] Immediate_field_write,
  input  [4:0] Write_register_write,
  input  [4:0] Write_register_write_2,
  input  Clock,
  output [31:0] Incremented_PC_read,
  output [31:0] Register_read_data_1_write_2,
  output [31:0] Register_read_data_2_read,
  output [31:0] Immediate_field_write_2,
  output [4:0] Write_register_read,
  output [4:0] Write_register_read_2
);

  Register #(.width(32)) Incremented_PC (
    .D(Incremented_PC_write), .Q(Incremented_PC_read), .clk(Clock));  // open: en, clr
  Register #(.width(32)) Register_read_data_1 (
    .D(Register_read_data_1_write), .Q(Register_read_data_1_write_2), .clk(Clock));  // open: en, clr
  Register #(.width(32)) Register_read_data_2 (
    .D(Register_read_data_2_write), .Q(Register_read_data_2_read), .clk(Clock));  // open: en, clr
  Register #(.width(32)) Immediate_field (
    .D(Immediate_field_write), .Q(Immediate_field_write_2), .clk(Clock));  // open: en, clr
  Register #(.width(5)) Write_register (
    .D(Write_register_write), .Q(Write_register_read), .clk(Clock));  // open: en, clr
  Register #(.width(5)) Write_register_2 (
    .D(Write_register_write_2), .Q(Write_register_read_2), .clk(Clock));  // open: en, clr
endmodule

module instructionDecode (
  input  [31:0] _32_bit_instruction,
  output [5:0] _26_31,
  output [4:0] _21_25,
  output [4:0] _16_20,
  output [15:0] _0_15,
  output [4:0] _11_15,
  output [5:0] _0_5
);


  assign _0_5 = _32_bit_instruction[5:0];
  assign _0_15 = _32_bit_instruction[15:0];
  assign _11_15 = _32_bit_instruction[15:11];
  assign _16_20 = _32_bit_instruction[20:16];
  assign _21_25 = _32_bit_instruction[25:21];
  assign _26_31 = _32_bit_instruction[31:26];
endmodule

module EX_MEM (
  input  [31:0] Branch_address_write,
  input  Zero_write,
  input  [31:0] Register_read_data_2_write,
  input  [31:0] in_4,
  input  [4:0] Write_register_write,
  input  Clock,
  output [31:0] Branch_address_read,
  output Zero_read,
  output [31:0] Register_read_data_2_read,
  output [31:0] out_10,
  output [4:0] Write_register_read
);

  Register #(.width(32)) Branch_address (
    .D(Branch_address_write), .Q(Branch_address_read), .clk(Clock));  // open: en, clr
  Register #(.width(1)) Zero (.D(Zero_write), .Q(Zero_read), .clk(Clock));  // open: en, clr
  Register #(.width(32)) Register_read_data_2 (
    .D(Register_read_data_2_write), .Q(Register_read_data_2_read), .clk(Clock));  // open: en, clr
  Register #(.width(32)) register_1 (.D(in_4), .Q(out_10), .clk(Clock));  // open: en, clr
  Register #(.width(5)) Write_register (
    .D(Write_register_write), .Q(Write_register_read), .clk(Clock));  // open: en, clr
endmodule

module MEM_WB (
  input  [31:0] Read_data_write,
  input  [31:0] ALU_result_write,
  input  [4:0] Write_register_write,
  input  Clock,
  output [31:0] Read_data_write_2,
  output [31:0] ALU_result_read,
  output [4:0] Write_register_read
);

  Register #(.width(32)) Read_data (.D(Read_data_write), .Q(Read_data_write_2), .clk(Clock));  // open: en, clr
  Register #(.width(32)) ALU_result (.D(ALU_result_write), .Q(ALU_result_read), .clk(Clock));  // open: en, clr
  Register #(.width(5)) Write_register (
    .D(Write_register_write), .Q(Write_register_read), .clk(Clock));  // open: en, clr
endmodule

module control (
  input  [5:0] Opcode,
  output [1:0] ALUOp,
  output Branch,
  output MemWrite,
  output MemRead,
  output RegWrite,
  output MemtoReg,
  output ALUSrc,
  output RegDst
);

  // PLA Control: pin names not known; wires that end beside it: Opcode, {RegDst, ALUSrc, MemtoReg, RegWrite, MemRead, MemWrite, Branch, ALUOp}
endmodule

module ALU_control (
  input  [5:0] Funct_field,
  input  [1:0] ALUOp,
  output [3:0] out_3
);

  wire [7:0] adder_1_out, bit_extender_1_out, bit_extender_2_out, shifter_1_out;

  assign bit_extender_1_out = {{6{1'b0}}, ALUOp};  // Bit_Extender bit_extender_1
  assign bit_extender_2_out = {{2{1'b0}}, Funct_field};  // Bit_Extender bit_extender_2
  Shifter shifter_1 (.in(bit_extender_1_out), .\dist (3'b110), .out(shifter_1_out));
  Adder adder_1 (.a(bit_extender_2_out), .b(shifter_1_out), .out(adder_1_out));  // open: cin, cout
  // PLA ALUControlPLA: pin names not known; wires that end beside it: adder_1_out, out_3
endmodule

module EX_ctrl (
  input  RegDst_write,
  input  [1:0] ALUSOp_write,
  input  ALUSrc_write,
  input  Clock,
  output RegDst_read,
  output [1:0] ALUOp_read,
  output ALUSrc_read
);

  Register #(.width(1)) RegDst (.D(RegDst_write), .Q(RegDst_read), .clk(Clock));  // open: en, clr
  Register #(.width(2)) ALUOp (.D(ALUSOp_write), .Q(ALUOp_read), .clk(Clock));  // open: en, clr
  Register #(.width(1)) ALUSrc (.D(ALUSrc_write), .Q(ALUSrc_read), .clk(Clock));  // open: en, clr
endmodule

module M_ctrl (
  input  Branch_write,
  input  MemWrite_write,
  input  MemRead_write,
  input  Clock,
  output Branch_read,
  output MemWrite_read,
  output MemRead_read
);

  Register #(.width(1)) Branch (.D(Branch_write), .Q(Branch_read), .clk(Clock));  // open: en, clr
  Register #(.width(1)) MemWrite (.D(MemWrite_write), .Q(MemWrite_read), .clk(Clock));  // open: en, clr
  Register #(.width(1)) MemRead (.D(MemRead_write), .Q(MemRead_read), .clk(Clock));  // open: en, clr
endmodule

module WB_ctrl (
  input  RegWrite_write,
  input  MemtoReg_write,
  input  Clock,
  output RegWrite_read,
  output MemtoReg_read
);

  Register #(.width(1)) RegWrite (.D(RegWrite_write), .Q(RegWrite_read), .clk(Clock));  // open: en, clr
  Register #(.width(1)) MemtoReg (.D(MemtoReg_write), .Q(MemtoReg_read), .clk(Clock));  // open: en, clr
endmodule

module Forwarding_uni (
  input  EX_MEM_RegWrite,
  input  [4:0] EX_MEM_Rd,
  input  [4:0] ID_EX_Rs,
  input  [4:0] ID_EX_Rt,
  input  [4:0] MEM_WB_Rd,
  input  MEM_WB_RegWrite,
  output [1:0] Forward_A,
  output [1:0] Forward_B
);

  wire bit_extender_3_out, bit_extender_4_out, bit_extender_5_out, bit_extender_6_out;
  wire [4:0] and_1_out, and_2_out, and_3_out, and_4_out, and_5_out, and_6_out, and_7_out, and_8_out,
       bit_extender_1_out, bit_extender_2_out, nand_1_out, nand_2_out;

  assign bit_extender_1_out = {{4{1'b0}}, EX_MEM_RegWrite};  // Bit_Extender bit_extender_1
  assign bit_extender_2_out = {{4{1'b0}}, MEM_WB_RegWrite};  // Bit_Extender bit_extender_2
  assign nand_1_out = ~(EX_MEM_Rd & {5{1'b0}});  // NAND_Gate nand_1, 5 bits wide
  assign and_1_out = EX_MEM_Rd & ID_EX_Rs;  // AND_Gate and_1, 5 bits wide
  assign and_2_out = EX_MEM_Rd & ID_EX_Rt;  // AND_Gate and_2, 5 bits wide
  assign and_3_out = ID_EX_Rt & MEM_WB_Rd;  // AND_Gate and_3, 5 bits wide
  assign and_4_out = ID_EX_Rs & MEM_WB_Rd;  // AND_Gate and_4, 5 bits wide
  assign nand_2_out = ~(MEM_WB_Rd & {5{1'b0}});  // NAND_Gate nand_2, 5 bits wide
  assign and_5_out = bit_extender_1_out & nand_1_out & and_1_out;  // AND_Gate and_5, 5 bits wide
  assign and_6_out = bit_extender_1_out & nand_1_out & and_2_out;  // AND_Gate and_6, 5 bits wide
  assign and_7_out = and_3_out & nand_2_out & bit_extender_2_out;  // AND_Gate and_7, 5 bits wide
  assign and_8_out = and_4_out & nand_2_out & bit_extender_2_out;  // AND_Gate and_8, 5 bits wide
  Bit_Extender #(.in_width(5), .out_width(1)) bit_extender_3 (.in(and_5_out), .out(bit_extender_3_out));
  Bit_Extender #(.in_width(5), .out_width(1)) bit_extender_4 (.in(and_6_out), .out(bit_extender_4_out));
  Bit_Extender #(.in_width(5), .out_width(1)) bit_extender_5 (.in(and_7_out), .out(bit_extender_5_out));
  Bit_Extender #(.in_width(5), .out_width(1)) bit_extender_6 (.in(and_8_out), .out(bit_extender_6_out));
  Multiplexer #(.width(2), .enable("false")) multiplexer_1 (
    .in0(2'b00), .in1(2'b10), .out(Forward_A), .sel(bit_extender_3_out));
  Multiplexer #(.width(2), .enable("false")) multiplexer_2 (
    .in0(2'b00), .in1(2'b10), .out(Forward_B), .sel(bit_extender_4_out));
  Multiplexer #(.width(2), .enable("false")) multiplexer_3 (
    .in0(2'b00), .in1(2'b01), .out(Forward_B), .sel(bit_extender_5_out));
  Multiplexer #(.width(2), .enable("false")) multiplexer_4 (
    .in0(2'b00), .in1(2'b01), .out(Forward_A), .sel(bit_extender_6_out));
endmodule

module alu_control (
  input  [5:0] Funct_field,
  input  [1:0] ALUOp,
  output [3:0] out_3
);

  wire [7:0] adder_1_out, bit_extender_1_out, bit_extender_2_out, shifter_1_out;

  assign bit_extender_1_out = {{6{1'b0}}, ALUOp};  // Bit_Extender bit_extender_1
  assign bit_extender_2_out = {{2{1'b0}}, Funct_field};  // Bit_Extender bit_extender_2
  Shifter shifter_1 (.in(bit_extender_1_out), .\dist (3'b110), .out(shifter_1_out));
  Adder adder_1 (.a(bit_extender_2_out), .b(shifter_1_out), .out(adder_1_out));  // open: cin, cout
  // PLA ALUControlPLA: pin names not known; wires that end beside it: adder_1_out, out_3
endmodule
